# Fritzing sketch circuit (saved by Fritzing 0.7.4b)
perfboards: 1

parts:
  Arduino1 = Arduino
  MOSFET = Basic FET N-Channel [package="TO220 [THT]"]
  LED_STRIPE = LED - 3mm [color="Red (633nm)" package="3 mm [THT]"]
  R1 = Resistor [tolerance=±5% resistance=470 package=THT]
  R2 = Resistor [tolerance=±5% resistance=1k package=THT]
  Video_Out = female pin header, 2 pins [form="♀ (female)"]
  J2 = Screw terminal - 2 pins [package=THT]
  +_12_V_IN = Screw terminal - 2 pins [package=THT]
  Joystick_connector_(DB_9) = DB25M

nets:
  N1: Arduino1.GND, MOSFET.drain, Video_Out.pin2, +_12_V_IN.pin2, Joystick_connector_(DB_9).pin8
  N2: Arduino1.D9, R2.Pin_0
  N3: Arduino1.D7, R1.Pin_0
  N4: Arduino1.D5, Joystick_connector_(DB_9).pin1
  N5: Arduino1.D4, Joystick_connector_(DB_9).pin2
  N6: Arduino1.D3, MOSFET.gate
  N7: Arduino1.D2, Joystick_connector_(DB_9).pin6
  N8: MOSFET.source, LED_STRIPE.cathode, J2.pin1
  N9: LED_STRIPE.anode, J2.pin2, +_12_V_IN.pin1
  N10: R1.Pin_1, R2.Pin_1, Video_Out.pin1

notes:
  12 V in
  to LED stripe
  composite out
